// Logisim project adders.circ as structural Verilog: 1 circuit, main circuit main
module main (
  input  in_1,
  input  in_2,
  input  in_3,
  input  in_4,
  input  [3:0] Num_1,
  input  [3:0] Num_2,
  output S0,
  output S1,
  output S2,
  output S3,
  output Cout
);

  wire and_1_out, clock_1_out, clock_2_out, clock_3_out, clock_4_out, nand_1_out, nand_2_out, nand_3_out,
       nand_4_out, nand_5_out, nand_6_out, nand_7_out, nand_8_out, nand_9_out, nand_10_out, nand_11_out,
       nand_12_out, nand_13_out, nand_14_out, nand_15_out, nand_16_out, nand_17_out, nand_18_out,
       nand_19_out, nand_20_out, nand_21_out, nand_22_out, nand_23_out, nand_24_out, nand_25_out,
       nand_26_out, nand_27_out, nand_29_out, nand_30_out, nand_31_out, nand_32_out, nand_33_out,
       nand_34_out, nand_35_out, nand_36_out, nand_37_out, nand_38_out, nand_39_out, nand_40_out,
       nand_42_out, nand_44_out, xor_1_out;

  Clock #(.highDuration(4), .lowDuration(4)) clock_1 (.out(clock_1_out));
  Clock #(.highDuration(2), .lowDuration(2)) clock_2 (.out(clock_2_out));
  nand nand_1 (nand_1_out, in_3, in_4);
  nand nand_2 (nand_2_out, clock_1_out, clock_2_out);
  xor xor_1 (xor_1_out, in_1, in_2);
  and and_1 (and_1_out, in_2, in_1);
  nand nand_3 (nand_3_out, in_3, nand_1_out);
  nand nand_4 (nand_4_out, nand_1_out, in_4);
  nand nand_5 (nand_5_out, clock_1_out, nand_2_out);
  nand nand_6 (nand_6_out, nand_2_out, clock_2_out);
  LED led_1 (.in(xor_1_out));
  LED led_2 (.in(and_1_out));
  nand nand_7 (nand_7_out, nand_3_out, nand_4_out);
  nand nand_8 (nand_8_out, nand_1_out, nand_1_out);
  LED led_3 (.in(nand_7_out));
  LED led_4 (.in(nand_8_out));
  nand nand_9 (nand_9_out, nand_5_out, nand_6_out);
  Clock clock_3 (.out(clock_3_out));
  nand nand_10 (nand_10_out, nand_9_out, clock_3_out);
  nand nand_11 (nand_11_out, Num_1[0], Num_2[0]);
  nand nand_12 (nand_12_out, Num_1[1], Num_2[1]);
  nand nand_13 (nand_13_out, Num_1[2], Num_2[2]);
  nand nand_14 (nand_14_out, Num_1[3], Num_2[3]);
  nand nand_15 (nand_15_out, nand_9_out, nand_10_out);
  nand nand_16 (nand_16_out, nand_10_out, clock_3_out);
  nand nand_17 (nand_17_out, Num_1[0], nand_11_out);
  nand nand_18 (nand_18_out, nand_11_out, Num_2[0]);
  nand nand_19 (nand_19_out, Num_1[1], nand_12_out);
  nand nand_20 (nand_20_out, nand_12_out, Num_2[1]);
  nand nand_21 (nand_21_out, Num_1[2], nand_13_out);
  nand nand_22 (nand_22_out, nand_13_out, Num_2[2]);
  nand nand_23 (nand_23_out, Num_1[3], nand_14_out);
  nand nand_24 (nand_24_out, nand_14_out, Num_2[3]);
  nand nand_25 (nand_25_out, nand_11_out, nand_11_out);
  nand nand_26 (nand_26_out, nand_15_out, nand_16_out);
  nand nand_27 (nand_27_out, nand_10_out, nand_2_out);
  nand nand_28 (S0, nand_17_out, nand_18_out);
  nand nand_29 (nand_29_out, nand_19_out, nand_20_out);
  nand nand_30 (nand_30_out, nand_21_out, nand_22_out);
  nand nand_31 (nand_31_out, nand_23_out, nand_24_out);
  LED led_5 (.in(nand_26_out));
  LED led_6 (.in(nand_27_out));
  Clock clock_4 (.out(clock_4_out));
  nand nand_32 (nand_32_out, nand_29_out, nand_25_out);
  nand nand_33 (nand_33_out, nand_30_out, nand_42_out);
  nand nand_34 (nand_34_out, nand_31_out, nand_44_out);
  // Digital_Oscilloscope digital_oscilloscope_1: pin names not known; wires that end beside it: clock_4_out, nand_26_out, nand_27_out
  nand nand_35 (nand_35_out, nand_29_out, nand_32_out);
  nand nand_36 (nand_36_out, nand_32_out, nand_25_out);
  nand nand_37 (nand_37_out, nand_30_out, nand_33_out);
  nand nand_38 (nand_38_out, nand_33_out, nand_42_out);
  nand nand_39 (nand_39_out, nand_31_out, nand_34_out);
  nand nand_40 (nand_40_out, nand_34_out, nand_44_out);
  nand nand_41 (S1, nand_35_out, nand_36_out);
  nand nand_42 (nand_42_out, nand_32_out, nand_12_out);
  nand nand_43 (S2, nand_37_out, nand_38_out);
  nand nand_44 (nand_44_out, nand_33_out, nand_13_out);
  nand nand_45 (S3, nand_39_out, nand_40_out);
  nand nand_46 (Cout, nand_34_out, nand_14_out);

  // Notes on the sheet:
  //   +
  //   sum
  //   carry
  //   sum
  //   carry
  //   Half adder using XOR and AND gates
  //   4-bit adder
  //   Half adder using NAND gates
  //   Full adder using NAND gates
endmodule
